// Logisim project F18Lab6.circ as structural Verilog: 1 circuit, main circuit main
module main (
  input  [7:0] register_input,
  input  select_0_1,
  input  enable,
  input  clock,
  output [7:0] register_contents
);

  wire [6:0] rom_1_data;
  wire [7:0] adder_1_out, multiplexer_1_out;
  wire [7:7] rom_1_data_2;

  Multiplexer #(.select(1), .width(8)) multiplexer_1 (
    .in0(adder_1_out), .in1(register_input), .out(multiplexer_1_out), .sel(select_0_1));
  Register #(.width(8), .trigger("rising")) register__PC (
    .D(multiplexer_1_out), .en(enable), .Q(register_contents), .clk(clock));  // open: clr
  Adder #(.width(8)) adder_1 (.a(register_contents), .b(8'h1), .out(adder_1_out));  // open: cin, cout
  TTY #(.rows(8), .cols(32), .trigger("rising")) tty_1 (.data(rom_1_data), .clk(clock), .we(1'b1));  // open: clr
  ROM #(.addrWidth(8), .dataWidth(8)) rom_1 (
    .addr(register_contents), .data({rom_1_data_2[7], rom_1_data}));  // open: sel

  // Notes on the sheet:
  //   8-bit adder
  //   contents of rom_1 (hex, n*v repeats v):
  //   43 6c 69 6d 61 74 65 20 63 68 61 6e 67 65 73 0 25
endmodule
